# Fritzing sketch servo an esp32 (saved by Fritzing 0.9.9b)

parts:
  M1 = Dagu DGServo 9g (Top view) [part_number=RS001B]
  A1 = Esp32-c3 super mini

nets:
  N1: M1.gnd, A1.Pin_15
  N2: M1.vcc, A1.Pin_16
  N3: M1.pulse, A1.Pin_2

custom parts:
  Esp32-c3 super mini: ESP32-C3 Development Board ESP32 SuperMini Development Board ESP32 Development Board WiFi Bluetooth.
